// Logisim project Hardware.circ as structural Verilog: 1 circuit, main circuit main
module main (
  input  Letter,
  input  in_2,
  input  Enable_Decrypt,
  input  E_1,
  input  in_5,
  input  N,
  input  in_7,
  input  in_8,
  input  in_9,
  output Output,
  output out_11,
  output out_12,
  output out_13
);

  wire button_1_out, clock_1_out, d_ff_1_q, d_ff_2_q, Load_out, multiplexer_3_out, multiplexer_4_out,
       multiplexer_5_out, multiplexer_6_out, multiplexer_9_out, multiplexer_10_out, not_1_out, not_2_out,
       or_1_out, Reset_out;
  wire [1:0] counter_1_q, multiplexer_2_out;
  wire [3:0] d_ff_6_q, multiplier_1_out;
  wire [3:1] divider_1_rem;

  Button button_1 (.out(button_1_out));
  Button Load (.out(Load_out));
  Multiplexer #(.enable("false")) multiplexer_1 (
    .in0(Letter), .in1(d_ff_1_q), .out(multiplexer_2_out[1]), .sel(Enable_Decrypt));
  Multiplexer #(.enable("false")) multiplexer_2 (
    .in0(in_2), .in1(d_ff_2_q), .out(multiplexer_2_out[0]), .sel(Enable_Decrypt));
  Multiplier #(.width(4)) multiplier_1 (
    .a({2'b00, multiplexer_2_out}), .b(d_ff_6_q), .out(multiplier_1_out));  // open: cin, cout
  D_Flip_Flop #(.trigger("falling")) d_ff_1 (
    .clk(button_1_out), .D(divider_1_rem[3]), .Q(d_ff_1_q));  // open: Qn, preset, en, reset
  Multiplexer #(.enable("false")) multiplexer_3 (
    .in0(multiplexer_2_out[0]), .in1(multiplier_1_out[0]), .out(multiplexer_3_out), .sel(not_1_out));
  Multiplexer #(.enable("false")) multiplexer_4 (
    .in0(multiplexer_2_out[1]), .in1(multiplier_1_out[1]), .out(multiplexer_4_out), .sel(not_1_out));
  Multiplexer #(.enable("false")) multiplexer_5 (
    .in0(1'b0), .in1(multiplier_1_out[2]), .out(multiplexer_5_out), .sel(not_1_out));
  Multiplexer #(.enable("false")) multiplexer_6 (
    .in0(1'b0), .in1(multiplier_1_out[3]), .out(multiplexer_6_out), .sel(not_1_out));
  D_Flip_Flop #(.trigger("falling")) d_ff_2 (
    .clk(button_1_out), .D(out_13), .Q(d_ff_2_q));  // open: Qn, preset, en, reset
  D_Flip_Flop #(.trigger("falling")) d_ff_3 (
    .clk(not_2_out), .D(multiplexer_6_out), .Q(d_ff_6_q[3]), .reset(Reset_out));  // open: Qn, preset, en
  not not_1 (not_1_out, Load_out);
  Multiplexer #(.enable("false")) multiplexer_7 (
    .in0(divider_1_rem[3]), .in1(divider_1_rem[1]), .out(Output), .sel(Enable_Decrypt));
  D_Flip_Flop #(.trigger("falling")) d_ff_4 (
    .clk(not_2_out), .D(multiplexer_5_out), .Q(d_ff_6_q[2]), .reset(Reset_out));  // open: Qn, preset, en
  Multiplexer #(.enable("false")) multiplexer_8 (
    .in0(divider_1_rem[1]), .in1(divider_1_rem[3]), .out(out_12), .sel(Enable_Decrypt));
  D_Flip_Flop #(.trigger("falling")) d_ff_5 (
    .clk(not_2_out), .D(multiplexer_4_out), .Q(d_ff_6_q[1]), .reset(Reset_out));  // open: Qn, preset, en
  not not_2 (not_2_out, multiplexer_9_out);
  D_Flip_Flop #(.trigger("falling")) d_ff_6 (
    .clk(not_2_out), .D(multiplexer_3_out), .Q(d_ff_6_q[0]), .reset(Reset_out));  // open: Qn, preset, en
  Counter #(.width(2), .max('h3)) counter_1 (
    .load(1'b1), .D({E_1, in_5}), .count(not_1_out), .Q(counter_1_q), .clk(multiplexer_9_out), .clr(Reset_out));  // open: carry
  Multiplexer #(.enable("false")) multiplexer_9 (
    .in0(multiplexer_10_out), .in1(Load_out), .out(multiplexer_9_out), .sel(Load_out));
  Button Reset (.out(Reset_out));
  Clock clock_1 (.out(clock_1_out));
  or or_1 (or_1_out, counter_1_q[0], counter_1_q[1]);
  Multiplexer #(.enable("false")) multiplexer_10 (
    .in0(1'b0), .in1(clock_1_out), .out(multiplexer_10_out), .sel(or_1_out));
  Divider #(.width(4)) divider_1 (
    .a(d_ff_6_q), .b({N, in_7, in_8, in_9}), .rem({divider_1_rem[3], out_11, divider_1_rem[1], out_13}));  // open: out, upper
endmodule
