// Logisim project MultiplierDiagram.circ as structural Verilog: 1 circuit, main circuit main
module main (
  input  [7:0] in_1,
  input  [7:0] in_2,
  input  [7:0] in_3,
  output [7:0] out_4,
  output [7:0] out_5
);

  wire [7:0] subtractor_1_out, subtractor_2_out;

  Multiplier multiplier_1 (.a(in_1), .b(in_2), .out(out_4));  // open: cin, cout
  Subtractor subtractor_1 (.a(in_1), .b(in_3), .out(subtractor_1_out));  // open: bin, bout
  Subtractor subtractor_2 (.a(in_2), .b(in_3), .out(subtractor_2_out));  // open: bin, bout
  Multiplier multiplier_2 (.a(subtractor_1_out), .b(subtractor_2_out), .out(out_5));  // open: cin, cout

  // Notes on the sheet:
  //   P
  //   Q
  //   n
  //   phi
endmodule
