// Logisim project RSA-AUTO.circ as structural Verilog: 4 circuits, main circuit main
module KeyGenerator (
  input  [7:0] Prime1_p,
  input  [7:0] Prime2_q,
  input  Reset,
  output [7:0] N,
  output [7:0] E,
  output [7:0] D
);

  wire clock_1_out, clock_2_out, multiplexer_1_out, multiplexer_2_out, not_1_out, or_1_out, or_2_out,
       or_3_out;
  wire [7:0] adder_1_out, counter_1_q, divider_1_rem, divider_2_rem, multiplier_2_out, multiplier_3_out,
       subtractor_1_out, subtractor_2_out;

  Multiplier multiplier_1 (.a(Prime1_p), .b(Prime2_q), .out(N));  // open: cin, cout
  Subtractor subtractor_1 (.a(Prime1_p), .b(8'h1), .out(subtractor_1_out));  // open: bin, bout
  Subtractor subtractor_2 (.a(Prime2_q), .b(8'h1), .out(subtractor_2_out));  // open: bin, bout
  Multiplexer multiplexer_1 (.in0(1'b0), .in1(clock_1_out), .out(multiplexer_1_out), .sel(or_3_out));  // open: en
  Clock clock_1 (.out(clock_1_out));
  Multiplier multiplier_2 (.a(subtractor_1_out), .b(subtractor_2_out), .out(multiplier_2_out));  // open: cin, cout
  Multiplexer multiplexer_2 (.in0(clock_2_out), .in1(1'b0), .out(multiplexer_2_out), .sel(or_2_out));  // open: en
  Clock clock_2 (.out(clock_2_out));
  Counter #(.behavior("old")) counter_1 (
    .Q(counter_1_q), .clk(multiplexer_1_out), .clr(or_1_out));  // open: load, D, count, carry, preset
  or or_1 (or_1_out, Reset, not_1_out);
  Counter #(.trigger("falling"), .behavior("old")) counter_2 (
    .Q(E), .clk(multiplexer_2_out), .clr(Reset));  // open: load, D, count, carry, preset
  Multiplier multiplier_3 (.a(multiplier_2_out), .b(counter_1_q), .out(multiplier_3_out));  // open: cin, cout
  not not_1 (not_1_out, or_2_out);
  Adder adder_1 (.a(multiplier_3_out), .b(8'h1), .out(adder_1_out));  // open: cin, cout
  Divider divider_1 (.a(multiplier_2_out), .b(E), .rem(divider_1_rem));  // open: out, upper
  Divider divider_2 (.a(adder_1_out), .b(E), .out(D), .rem(divider_2_rem));  // open: upper
  or or_2 (or_2_out, divider_1_rem[0], divider_1_rem[1], divider_1_rem[2], divider_1_rem[3], divider_1_rem[4], divider_1_rem[5], divider_1_rem[6], divider_1_rem[7]);
  or or_3 (or_3_out, divider_2_rem[0], divider_2_rem[1], divider_2_rem[2], divider_2_rem[3], divider_2_rem[4], divider_2_rem[5], divider_2_rem[6], divider_2_rem[7]);

  // Notes on the sheet:
  //   K
  //   Phi=(p-1)*(q-1)
endmodule

module Encrypter (
  input  [6:0] Letter,
  input  [7:0] E,
  input  Reset,
  input  [7:0] N,
  input  Load,
  output [7:0] Encyrpted
);

  wire clock_1_out, multiplexer_2_out, multiplexer_3_out, not_1_out, or_1_out;
  wire [6:0] subtractor_2_out;
  wire [7:0] counter_1_q, subtractor_1_out;
  wire [25:0] bit_extender_1_out, bit_extender_2_out, divider_1_rem, multiplexer_1_out, multiplier_1_out,
       register_1_q;

  Subtractor subtractor_1 (.a(E), .b(8'h1), .out(subtractor_1_out));  // open: bin, bout
  Subtractor #(.width(7)) subtractor_2 (.a(Letter), .b(7'b1100001), .out(subtractor_2_out));  // open: bin, bout
  assign bit_extender_1_out = {{19{1'b0}}, subtractor_2_out};  // Bit_Extender bit_extender_1
  Multiplier #(.width(26)) multiplier_1 (
    .a(bit_extender_1_out), .b(register_1_q), .out(multiplier_1_out));  // open: cin, cout
  Multiplexer #(.width(26)) multiplexer_1 (
    .in0(bit_extender_1_out), .in1(multiplier_1_out), .out(multiplexer_1_out), .sel(not_1_out));  // open: en
  not not_1 (not_1_out, Load);
  Register #(.width(26), .trigger("falling"), .Select("low")) register_1 (
    .D(multiplexer_1_out), .Q(register_1_q), .clk(multiplexer_2_out), .clr(Reset));  // open: en
  assign bit_extender_2_out = {{18{1'b0}}, N};  // Bit_Extender bit_extender_2
  Multiplexer multiplexer_2 (.in0(multiplexer_3_out), .in1(Load), .out(multiplexer_2_out), .sel(Load));  // open: en
  Divider #(.width(26)) divider_1 (.a(register_1_q), .b(bit_extender_2_out), .rem(divider_1_rem));  // open: out, upper
  Multiplexer multiplexer_3 (.in0(1'b0), .in1(clock_1_out), .out(multiplexer_3_out), .sel(or_1_out));  // open: en
  Counter #(.behavior("old")) counter_1 (
    .load(1'b1), .D(subtractor_1_out), .count(not_1_out), .Q(counter_1_q), .clk(multiplexer_2_out),
    .clr(Reset));  // open: carry, preset
  Bit_Extender #(.in_width(26), .out_width(8), .\type ("zero")) bit_extender_3 (.in(divider_1_rem), .out(Encyrpted));
  Clock clock_1 (.out(clock_1_out));
  or or_1 (or_1_out, counter_1_q[0], counter_1_q[1], counter_1_q[2], counter_1_q[3], counter_1_q[4], counter_1_q[5], counter_1_q[6], counter_1_q[7]);
endmodule

module Decrypter (
  input  [7:0] Encypted_Data,
  input  [7:0] D,
  input  Reset,
  input  [7:0] N,
  input  Load,
  output [6:0] out_6
);

  wire clock_1_out, multiplexer_2_out, multiplexer_3_out, not_1_out, or_1_out;
  wire [6:0] bit_extender_3_out;
  wire [7:0] counter_1_q, subtractor_1_out;
  wire [25:0] bit_extender_1_out, bit_extender_2_out, divider_1_rem, multiplexer_1_out, multiplier_1_out,
       register_1_q;

  Subtractor subtractor_1 (.a(D), .b(8'h1), .out(subtractor_1_out));  // open: bin, bout
  assign bit_extender_1_out = {{18{1'b0}}, Encypted_Data};  // Bit_Extender bit_extender_1
  Multiplier #(.width(26)) multiplier_1 (
    .a(bit_extender_1_out), .b(register_1_q), .out(multiplier_1_out));  // open: cin, cout
  Multiplexer #(.width(26)) multiplexer_1 (
    .in0(bit_extender_1_out), .in1(multiplier_1_out), .out(multiplexer_1_out), .sel(not_1_out));  // open: en
  not not_1 (not_1_out, Load);
  Multiplexer multiplexer_2 (.in0(multiplexer_3_out), .in1(Load), .out(multiplexer_2_out), .sel(Load));  // open: en
  Register #(.width(26), .trigger("falling"), .Select("low")) register_1 (
    .D(multiplexer_1_out), .Q(register_1_q), .clk(multiplexer_2_out), .clr(Reset));  // open: en
  assign bit_extender_2_out = {{18{1'b0}}, N};  // Bit_Extender bit_extender_2
  Multiplexer multiplexer_3 (.in0(1'b0), .in1(clock_1_out), .out(multiplexer_3_out), .sel(or_1_out));  // open: en
  Counter #(.behavior("old")) counter_1 (
    .load(1'b1), .D(subtractor_1_out), .count(not_1_out), .Q(counter_1_q), .clk(multiplexer_2_out),
    .clr(Reset));  // open: carry, preset
  Divider #(.width(26)) divider_1 (.a(register_1_q), .b(bit_extender_2_out), .rem(divider_1_rem));  // open: out, upper
  Clock clock_1 (.out(clock_1_out));
  Bit_Extender #(.in_width(26), .out_width(7), .\type ("zero")) bit_extender_3 (
    .in(divider_1_rem), .out(bit_extender_3_out));
  Adder #(.width(7)) adder_1 (.a(bit_extender_3_out), .b(7'b1100001), .out(out_6));  // open: cin, cout
  or or_1 (or_1_out, counter_1_q[0], counter_1_q[1], counter_1_q[2], counter_1_q[3], counter_1_q[4], counter_1_q[5], counter_1_q[6], counter_1_q[7]);
endmodule

module main (
  input  [7:0] Prime1,
  input  [7:0] Prime2,
  output [7:0] Cipher_Text,
  output [7:0] out_4
);

  wire button_1_out, Clear_out, Load_2_out, Load_out, not_1_out, Reset_2_out, Reset_3_out, Reset_All_out,
       Reset_out, Write_out, xor_1_out, xor_2_out, xor_3_out;
  wire [6:0] decrypter_1_out_6, keyboard_1_data;
  wire [7:0] keygenerator_1_d, keygenerator_1_n;

  Button Reset (.out(Reset_out));
  xor xor_1 (xor_1_out, Reset_out, Reset_All_out);
  KeyGenerator keygenerator_1 (
    .Prime1_p(Prime1), .Prime2_q(Prime2), .Reset(xor_1_out), .N(keygenerator_1_n), .E(out_4),
    .D(keygenerator_1_d));
  Button button_1 (.out(button_1_out));
  Keyboard #(.buflen(1)) keyboard_1 (.clk(button_1_out), .data(keyboard_1_data));  // open: re, clr, avail
  Button Reset_All (.out(Reset_All_out));
  Button Load (.out(Load_out));
  Button Reset_2 (.out(Reset_2_out));
  Button Load_2 (.out(Load_2_out));
  Button Reset_3 (.out(Reset_3_out));
  xor xor_2 (xor_2_out, Reset_All_out, Reset_2_out);
  Encrypter encrypter_1 (
    .Letter(keyboard_1_data), .E(out_4), .N(keygenerator_1_n), .Load(Load_out), .Encyrpted(Cipher_Text),
    .Reset(xor_2_out));
  xor xor_3 (xor_3_out, Reset_All_out, Reset_3_out);
  Decrypter decrypter_1 (
    .Encypted_Data(Cipher_Text), .D(keygenerator_1_d), .N(keygenerator_1_n), .Load(Load_2_out),
    .out_6(decrypter_1_out_6), .Reset(xor_3_out));
  TTY #(.rows(1), .cols(1)) tty_1 (.data(decrypter_1_out_6), .clk(Write_out), .we(not_1_out), .clr(Clear_out));
  not not_1 (not_1_out, Clear_out);
  Button Write (.out(Write_out));
  Button Clear (.out(Clear_out));

  // Notes on the sheet:
  //   (Proof Of Concept)
  //   Instructions for Operation:
  //   2. Press the reset button,to generate key.
  //   3. Enter the letter to be encrypted.
  //   Key Generator
  //   RSA Implementation
  //   1. First enter two prime numbers as 8-bit binary .
  //   5. To write into the terminal press the write button(you can always use the clear button to flush the terminal)
  //   Enter input here
  //   4. Reset and load (wait for the output for about 2 seconds). If the output does not show (except for the case of 'a'), press load again.
  //   Encrypter
  //   Decrypter
  //   Decrypted text
endmodule
