// Logisim project RSA.circ as structural Verilog: 4 circuits, main circuit main
module main (
  input  Load,
  input  [7:0] Prime1,
  input  [7:0] Prime2,
  input  Load_2,
  output [7:0] Encrypted_Data_Cipher_Text,
  output [7:0] Count,
  output [7:0] Count_2
);

  wire button_1_out, Button_2_out, Button_3_out, Clear_out, E_button_out, K_button_out, keygenerator_1_rem1,
       keygenerator_1_rem2, not_1_out, not_2_out, not_3_out, not_4_out, not_5_out, Reset_2_out, Reset_D_out,
       Reset_E_out, Reset_out, Write_out;
  wire [6:0] decrypter_1_letter, keyboard_1_data;
  wire [7:0] keygenerator_1_d, keygenerator_1_e, keygenerator_1_n;

  Button E_button (.out(E_button_out));
  Button K_button (.out(K_button_out));
  Button Reset_E (.out(Reset_E_out));
  Button Reset_D (.out(Reset_D_out));
  not not_1 (not_1_out, Reset_E_out);
  not not_2 (not_2_out, Reset_D_out);
  KeyGenerator keygenerator_1 (
    .Prime1_p(Prime1), .Prime2_q(Prime2), .E_button(E_button_out), .K_Button(K_button_out),
    .Reset_E(not_1_out), .Reset_D(not_2_out), .N(keygenerator_1_n), .E(keygenerator_1_e),
    .D(keygenerator_1_d), .Rem1(keygenerator_1_rem1), .Rem2(keygenerator_1_rem2));
  LED Rem1 (.in(keygenerator_1_rem1));
  LED Rem2 (.in(keygenerator_1_rem2));
  Button button_1 (.out(button_1_out));
  Keyboard keyboard_1 (.clk(button_1_out), .data(keyboard_1_data));  // open: re, clr, avail
  Button Reset (.out(Reset_out));
  not not_3 (not_3_out, Reset_out);
  Button Button_2 (.out(Button_2_out));
  Button Button_3 (.out(Button_3_out));
  Button Reset_2 (.out(Reset_2_out));
  Encrypter encrypter_1 (
    .Letter(keyboard_1_data), .E(keygenerator_1_e), .N(keygenerator_1_n), .Reset(not_3_out), .Load(Load),
    .Button(Button_2_out), .E_Count(Count), .Encyrpted(Encrypted_Data_Cipher_Text));
  Decrypter decrypter_1 (
    .Encrypted_Data(Encrypted_Data_Cipher_Text), .D(keygenerator_1_d), .N(keygenerator_1_n), .Load(Load_2),
    .Button(Button_3_out), .D_Count(Count_2), .Reset(not_4_out), .Letter(decrypter_1_letter));
  not not_4 (not_4_out, Reset_2_out);
  TTY tty_1 (.data(decrypter_1_letter), .clk(Write_out), .we(not_5_out), .clr(Clear_out));
  Button Write (.out(Write_out));
  not not_5 (not_5_out, Clear_out);
  Button Clear (.out(Clear_out));

  // Notes on the sheet:
  //   (Proof Of Concept)
  //   Instructions for Operation:
  //   4. Enter the letter to be encrypted.
  //   RSA Implementation
  //   1. First enter two prime numbers as 8-bit binary .
  //   Key Generator
  //   N
  //   6. Turn the load button off and repeatedly press the button untill count is zero.
  //   8. Turn the load button off and repeatedly press the button untill count is zero.
  //   E
  //   D
  //   2. Now press the E-button repeatedly till Rem1 turns on.(You can always use the Reset-E button to reset.)
  //   3. Now press the K-button repeatedly till Rem2 turns on.(You can always use the Reset-D button to reset.)
  //   5. Turn the load button and press the button once to load in the keys from the Key-Generation module.
  //   7. Turn the load button and press the button once to load in the keys from the Key-Generation module.
  //   9. To write into the terminal press the write button(you can always use the clear button to flush the terminal)
  //   Input Letter to be encrypted
  //   Encrypter
  //   Decrypter
endmodule

module KeyGenerator (
  input  [7:0] Prime1_p,
  input  [7:0] Prime2_q,
  input  E_button,
  input  K_Button,
  input  Reset_E,
  input  Reset_D,
  output [7:0] N,
  output [7:0] E,
  output [7:0] D,
  output Rem1,
  output Rem2
);

  wire not_1_out, not_2_out, or_2_out;
  wire [7:0] adder_1_out, counter_1_q, divider_1_rem, divider_2_rem, multiplier_2_out, multiplier_3_out,
       subtractor_1_out, subtractor_2_out;

  Multiplier multiplier_1 (.a(Prime1_p), .b(Prime2_q), .out(N));  // open: cin, cout
  Subtractor subtractor_1 (.a(Prime1_p), .b(8'h1), .out(subtractor_1_out));  // open: bin, bout
  Subtractor subtractor_2 (.a(Prime2_q), .b(8'h1), .out(subtractor_2_out));  // open: bin, bout
  Counter counter_1 (.Q(counter_1_q), .clk(K_Button), .clr(not_1_out));  // open: load, D, count, carry
  not not_1 (not_1_out, Reset_D);
  Multiplier multiplier_2 (.a(subtractor_1_out), .b(subtractor_2_out), .out(multiplier_2_out));  // open: cin, cout
  Counter #(.trigger("falling")) counter_2 (.Q(E), .clk(E_button), .clr(not_2_out));  // open: load, D, count, carry
  not not_2 (not_2_out, Reset_E);
  Multiplier multiplier_3 (.a(multiplier_2_out), .b(counter_1_q), .out(multiplier_3_out));  // open: cin, cout
  Adder adder_1 (.a(multiplier_3_out), .b(8'h1), .out(adder_1_out));  // open: cin, cout
  Divider divider_1 (.a(multiplier_2_out), .b(E), .rem(divider_1_rem));  // open: out, upper
  Divider divider_2 (.a(adder_1_out), .b(E), .out(D), .rem(divider_2_rem));  // open: upper
  or or_1 (Rem1, divider_1_rem[0], divider_1_rem[1], divider_1_rem[2], divider_1_rem[3], divider_1_rem[4], divider_1_rem[5], divider_1_rem[6], divider_1_rem[7]);
  or or_2 (or_2_out, divider_2_rem[0], divider_2_rem[1], divider_2_rem[2], divider_2_rem[3], divider_2_rem[4], divider_2_rem[5], divider_2_rem[6], divider_2_rem[7]);
  not not_3 (Rem2, or_2_out);

  // Notes on the sheet:
  //   K
  //   Phi=(p-1)*(q-1)
endmodule

module Encrypter (
  input  [6:0] Letter,
  input  [7:0] E,
  input  [7:0] N,
  input  Reset,
  input  Load,
  input  Button,
  output [7:0] Encyrpted,
  output [7:0] E_Count
);

  wire not_1_out, not_2_out;
  wire [6:0] subtractor_2_out;
  wire [7:0] subtractor_1_out;
  wire [25:0] bit_extender_1_out, bit_extender_2_out, divider_1_rem, multiplexer_1_out, multiplier_1_out,
       register_1_q;

  Subtractor subtractor_1 (.a(E), .b(8'h1), .out(subtractor_1_out));  // open: bin, bout
  Subtractor #(.width(7)) subtractor_2 (.a(Letter), .b(7'b1100001), .out(subtractor_2_out));  // open: bin, bout
  assign bit_extender_1_out = {{19{1'b0}}, subtractor_2_out};  // Bit_Extender bit_extender_1
  assign bit_extender_2_out = {{18{1'b0}}, N};  // Bit_Extender bit_extender_2
  Multiplier #(.width(26)) multiplier_1 (
    .a(bit_extender_1_out), .b(register_1_q), .out(multiplier_1_out));  // open: cin, cout
  not not_1 (not_1_out, Load);
  Multiplexer #(.width(26)) multiplexer_1 (
    .in0(bit_extender_1_out), .in1(multiplier_1_out), .out(multiplexer_1_out), .sel(not_1_out));  // open: en
  Register #(.width(26)) register_1 (
    .D(multiplexer_1_out), .Q(register_1_q), .clk(Button), .clr(not_2_out));  // open: en
  Counter counter_1 (
    .load(1'b1), .D(subtractor_1_out), .Q(E_Count), .clk(Button), .clr(not_2_out));  // open: count, carry
  Divider #(.width(26)) divider_1 (.a(register_1_q), .b(bit_extender_2_out), .rem(divider_1_rem));  // open: out, upper
  not not_2 (not_2_out, Reset);
  Bit_Extender #(.in_width(26), .out_width(8)) bit_extender_3 (.in(divider_1_rem), .out(Encyrpted));
endmodule

module Decrypter (
  input  [7:0] Encrypted_Data,
  input  [7:0] D,
  input  [7:0] N,
  input  Load,
  input  Button,
  input  Reset,
  output [6:0] Letter,
  output [7:0] D_Count
);

  wire not_1_out, not_2_out;
  wire [6:0] bit_extender_3_out;
  wire [7:0] subtractor_1_out;
  wire [25:0] bit_extender_1_out, bit_extender_2_out, divider_1_rem, multiplexer_1_out, multiplier_1_out,
       register_1_q;

  not not_1 (not_1_out, Load);
  assign bit_extender_1_out = {{18{1'b0}}, Encrypted_Data};  // Bit_Extender bit_extender_1
  Subtractor subtractor_1 (.a(D), .b(8'h1), .out(subtractor_1_out));  // open: bin, bout
  assign bit_extender_2_out = {{18{1'b0}}, N};  // Bit_Extender bit_extender_2
  Multiplier #(.width(26)) multiplier_1 (
    .a(bit_extender_1_out), .b(register_1_q), .out(multiplier_1_out));  // open: cin, cout
  Multiplexer #(.width(26)) multiplexer_1 (
    .in0(bit_extender_1_out), .in1(multiplier_1_out), .out(multiplexer_1_out), .sel(not_1_out));  // open: en
  Register #(.width(26)) register_1 (
    .D(multiplexer_1_out), .Q(register_1_q), .clk(Button), .clr(not_2_out));  // open: en
  not not_2 (not_2_out, Reset);
  Counter counter_1 (
    .load(1'b1), .D(subtractor_1_out), .count(not_1_out), .Q(D_Count), .clk(Button), .clr(not_2_out));  // open: carry
  Divider #(.width(26)) divider_1 (.a(register_1_q), .b(bit_extender_2_out), .rem(divider_1_rem));  // open: out, upper
  Bit_Extender #(.in_width(26), .out_width(7)) bit_extender_3 (.in(divider_1_rem), .out(bit_extender_3_out));
  Adder #(.width(7)) adder_1 (.a(bit_extender_3_out), .b(7'b1100001), .out(Letter));  // open: cin, cout
endmodule
