// Logisim project key.circ as structural Verilog: 1 circuit, main circuit main
module main (
  input  in_1,
  input  in_2,
  input  [3:0] P,
  input  [3:0] Q,
  input  [7:0] in_5,
  input  in_6,
  input  in_7,
  input  in_8,
  input  in_9,
  input  in_10,
  output [7:0] E_Count,
  output [7:0] Encyrpted,
  output [7:0] N,
  output [7:0] E,
  output [7:0] D,
  output [7:0] REM1,
  output [7:0] REM2,
  output [7:0] D_Count,
  output [15:0] K,
  output [7:0] Phi
);

  wire button_1_out, button_2_out, button_3_out, button_4_out, button_5_out, button_6_out, not_1_out,
       not_2_out, not_3_out, not_4_out, not_5_out;
  wire [6:0] adder_2_out, bit_extender_11_out, keyboard_1_data, subtractor_5_out;
  wire [7:0] bit_extender_1_out, bit_extender_2_out, subtractor_1_out, subtractor_2_out, subtractor_3_out,
       subtractor_4_out;
  wire [15:0] adder_1_out, bit_extender_3_out, bit_extender_4_out, divider_2_out, divider_2_rem,
       multiplier_3_out;
  wire [23:0] bit_extender_7_out, bit_extender_8_out, bit_extender_9_out, divider_3_rem, divider_4_rem,
       multiplexer_1_out, multiplexer_2_out, multiplier_4_out, multiplier_5_out, register_1_q, register_2_q;

  assign bit_extender_1_out = {{4{1'b0}}, P};  // Bit_Extender bit_extender_1
  assign bit_extender_2_out = {{4{1'b0}}, Q};  // Bit_Extender bit_extender_2
  Multiplier multiplier_1 (.a(bit_extender_1_out), .b(bit_extender_2_out), .out(N));  // open: cin, cout
  Subtractor subtractor_1 (.a(bit_extender_1_out), .b(8'h1), .out(subtractor_1_out));  // open: bin, bout
  Subtractor subtractor_2 (.a(bit_extender_2_out), .b(8'h1), .out(subtractor_2_out));  // open: bin, bout
  Multiplier multiplier_2 (.a(subtractor_1_out), .b(subtractor_2_out), .out(Phi));  // open: cin, cout
  assign bit_extender_3_out = {{8{1'b0}}, Phi};  // Bit_Extender bit_extender_3
  Counter #(.width(16), .max('hffff), .behavior("old")) counter_1 (
    .Q(K), .clk(button_1_out), .clr(not_2_out));  // open: load, D, count, carry, preset
  Button button_1 (.out(button_1_out));
  Counter #(.trigger("falling"), .behavior("old")) counter_2 (
    .Q(E), .clk(button_2_out), .clr(not_1_out));  // open: load, D, count, carry, preset
  not not_1 (not_1_out, in_6);
  Button button_2 (.out(button_2_out));
  Multiplier #(.width(16)) multiplier_3 (.a(bit_extender_3_out), .b(K), .out(multiplier_3_out));  // open: cin, cout
  not not_2 (not_2_out, in_8);
  Adder #(.width(16)) adder_1 (.a(multiplier_3_out), .b(16'h1), .out(adder_1_out));  // open: cin, cout
  Divider divider_1 (.a(Phi), .b(E), .rem(REM1));  // open: out, upper
  assign bit_extender_4_out = {{8{1'b0}}, E};  // Bit_Extender bit_extender_4
  Divider #(.width(16)) divider_2 (
    .a(adder_1_out), .b(bit_extender_4_out), .out(divider_2_out), .rem(divider_2_rem));  // open: upper
  Bit_Extender #(.in_width(16), .out_width(8), .\type ("zero")) bit_extender_5 (.in(divider_2_rem), .out(REM2));
  Bit_Extender #(.in_width(16), .out_width(8), .\type ("zero")) bit_extender_6 (.in(divider_2_out), .out(D));
  Keyboard keyboard_1 (.clk(button_3_out), .data(keyboard_1_data));  // open: re, clr, avail
  Button button_3 (.out(button_3_out));
  Subtractor subtractor_3 (.a(E), .b(8'h1), .out(subtractor_3_out));  // open: bin, bout
  Subtractor subtractor_4 (.a(D), .b(8'h1), .out(subtractor_4_out));  // open: bin, bout
  Subtractor #(.width(7)) subtractor_5 (
    .a(keyboard_1_data), .b(7'b1100001), .out(subtractor_5_out));  // open: bin, bout
  assign bit_extender_7_out = {{16{1'b0}}, Encyrpted};  // Bit_Extender bit_extender_7
  assign bit_extender_8_out = {{17{1'b0}}, subtractor_5_out};  // Bit_Extender bit_extender_8
  assign bit_extender_9_out = {{16{1'b0}}, N};  // Bit_Extender bit_extender_9
  Multiplier #(.width(24)) multiplier_4 (
    .a(bit_extender_8_out), .b(register_1_q), .out(multiplier_4_out));  // open: cin, cout
  Multiplier #(.width(24)) multiplier_5 (
    .a(bit_extender_7_out), .b(register_2_q), .out(multiplier_5_out));  // open: cin, cout
  Multiplexer #(.width(24)) multiplexer_1 (
    .in0(bit_extender_7_out), .in1(multiplier_5_out), .out(multiplexer_1_out), .sel(in_9));  // open: en
  Multiplexer #(.width(24)) multiplexer_2 (
    .in0(bit_extender_8_out), .in1(multiplier_4_out), .out(multiplexer_2_out), .sel(in_2));  // open: en
  Button button_4 (.out(button_4_out));
  Button button_5 (.out(button_5_out));
  Register #(.width(24), .Select("low")) register_1 (
    .D(multiplexer_2_out), .Q(register_1_q), .clk(button_4_out), .clr(not_3_out));  // open: en
  Divider #(.width(24)) divider_3 (.a(register_1_q), .b(bit_extender_9_out), .rem(divider_3_rem));  // open: out, upper
  Register #(.width(24), .Select("low")) register_2 (
    .D(multiplexer_1_out), .Q(register_2_q), .clk(button_5_out), .clr(not_4_out));  // open: en
  Counter #(.behavior("old")) counter_3 (
    .load(1'b1), .D(subtractor_4_out), .count(in_9), .Q(D_Count), .clk(button_5_out), .clr(not_4_out));  // open: carry, preset
  not not_3 (not_3_out, in_1);
  Counter #(.behavior("old")) counter_4 (
    .load(1'b1), .D(subtractor_3_out), .count(in_2), .Q(E_Count), .clk(button_4_out), .clr(not_3_out));  // open: carry, preset
  Bit_Extender #(.in_width(24), .out_width(8), .\type ("zero")) bit_extender_10 (.in(divider_3_rem), .out(Encyrpted));
  not not_4 (not_4_out, in_7);
  Divider #(.width(24)) divider_4 (.a(register_2_q), .b(bit_extender_9_out), .rem(divider_4_rem));  // open: out, upper
  Bit_Extender #(.in_width(24), .out_width(7), .\type ("zero")) bit_extender_11 (
    .in(divider_4_rem), .out(bit_extender_11_out));
  Adder #(.width(7)) adder_2 (.a(bit_extender_11_out), .b(7'b1100001), .out(adder_2_out));  // open: cin, cout
  TTY tty_1 (.data(adder_2_out), .clk(button_6_out), .we(in_10), .clr(not_5_out));
  not not_5 (not_5_out, in_10);
  Button button_6 (.out(button_6_out));
endmodule
